# Fritzing sketch autonomous_robot (saved by Fritzing 0.9.3b)
breadboards: 1

parts:
  Part1 = Arduino Uno (Rev3)
  M1 = DC Motor [part_number="left wheel (green = +)"]
  M2 = DC Motor [part_number="right wheel (yellow = +)"]
  S1 = H-Bridge with L298N
  VCC1 = 4 x AAA Battery Mount
  LED1 = RGB LED (com. anode, rbg) [package="5 mm [THT]"]
  R1 = Resistor [tolerance=±5% resistance=220 package="0805 [SMD]"]
  R2 = Resistor [tolerance=±5% resistance=220 package="0805 [SMD]"]
  hc-sr1 = hc-sr04
  J1 = Basic Servo

nets:
  N1: Part1.D8, S1.IN2
  N2: Part1.D10_PWM/SS, J1.pulse
  N3: Part1.D12/MISO, S1.IN3
  N4: Part1.D13/SCK, S1.IN4
  N5: Part1.D2, hc-sr1.Trig
  N6: Part1.D3_PWM, hc-sr1.Echo
  N7: Part1.D5_PWM, R1.Pin_0
  N8: Part1.D6_PWM, R2.Pin_1
  N9: Part1.D7, S1.IN1
  5V: Part1.5V, S1.5V
  GND: Part1.GND, S1.GND, VCC1.-, LED1.common_anode, hc-sr1.GND, J1.gnd
  N10: M1.pin_1, S1.OUT3-Motor2
  N11: M1.pin_2, S1.OUT4-Motor2
  N12: M2.pin_1, S1.OUT1-Motor1
  N13: M2.pin_2, S1.OUT2-Motor1
  VCC: S1.12V, VCC1.+, hc-sr1.VCC, J1.vcc
  N14: LED1.red_cathode, R1.Pin_1
  N15: LED1.blue_cathode, R2.Pin_0

notes:
  motor bridge: missing two enable pins outside of In1 an In4. connect to the pin closest to the edge of the board. see yellow wirres

custom parts:
  H-Bridge with L298N: h-bridge
